// Logisim project calucl 1.circ as structural Verilog: 1 circuit, main circuit main
module main (
  input  in_1,
  input  in_2,
  input  in_3,
  input  in_4,
  input  in_5,
  input  in_6,
  input  in_7,
  input  in_8
);

  wire _0, _1, _2, _3, _4, _5, _6, _7, _8, _9, and_1_out, and_2_out, and_11_out, and_12_out, and_13_out,
       and_14_out, and_15_out, and_16_out, and_17_out, and_18_out, and_19_out, and_20_out, and_21_out,
       and_22_out, and_23_out, and_24_out, and_25_out, and_26_out, and_27_out, and_28_out, and_29_out,
       and_30_out, and_31_out, and_32_out, and_33_out, and_34_out, and_35_out, and_36_out, and_37_out,
       and_38_out, and_39_out, and_40_out, and_41_out, and_42_out, and_43_out, and_44_out, and_45_out,
       and_46_out, and_47_out, and_48_out, and_49_out, and_50_out, and_51_out, and_52_out, and_53_out,
       and_54_out, and_55_out, and_56_out, and_57_out, and_58_out, and_59_out, and_60_out, and_61_out,
       and_62_out, and_63_out, and_64_out, and_65_out, and_66_out, and_67_out, and_68_out, and_69_out,
       and_70_out, and_71_out, and_72_out, and_73_out, and_74_out, and_75_out, and_76_out, and_77_out,
       and_78_out, and_79_out, and_80_out, and_81_out, and_82_out, and_83_out, and_84_out, and_85_out,
       and_86_out, and_87_out, and_88_out, and_89_out, and_90_out, and_91_out, and_92_out, and_93_out,
       and_94_out, and_95_out, and_96_out, and_97_out, and_98_out, and_99_out, and_100_out, and_101_out,
       and_102_out, and_103_out, and_104_out, and_105_out, and_106_out, and_107_out, and_108_out,
       and_109_out, and_110_out, and_111_out, and_112_out, and_113_out, and_114_out, and_119_out,
       and_120_out, and_121_out, and_122_out, and_123_out, and_124_out, and_125_out, and_126_out,
       and_127_out, and_128_out, and_129_out, and_130_out, and_131_out, and_132_out, and_133_out,
       and_134_out, b1, b2, b4, b8, b_plus, bt, c1, c2, c4, c8, ct, d_ff_1_q, d_ff_1_qn, d_ff_2_q, d_ff_3_q,
       d_ff_4_q, d_ff_5_q, d_ff_5_qn, d_ff_6_q, d_ff_7_q, d_ff_8_q, d_ff_8_qn, d_ff_9_q, d_ff_10_q,
       d_ff_11_q, d_ff_12_q, d_ff_13_q, d_ff_14_q, d_ff_15_q, d_ff_16_q, d_ff_17_q, d_ff_18_q, d_ff_19_q,
       d_ff_20_q, d_ff_20_qn, d_ff_21_qn, d_ff_22_q, d_ff_23_q, d_ff_24_q, d_ff_25_q, d_ff_25_qn, d_ff_26_q,
       d_ff_27_q, d_ff_28_q, d_ff_28_qn, d_ff_29_q, d_ff_30_q, d_ff_31_q, d_ff_32_q, d_ff_33_q, d_ff_34_q,
       d_ff_35_q, d_ff_36_q, d_ff_38_q, d_ff_39_q, d_ff_39_qn, d_ff_40_q, d_ff_41_q, d_ff_42_q, d_ff_43_q,
       d_ff_44_q, d_ff_44_qn, d_ff_45_q, d_ff_46_q, d_ff_47_q, d_ff_48_q, d_ff_49_q, d_ff_49_qn, d_ff_50_q,
       d_ff_51_q, d_ff_52_q, d_ff_53_q, dt, fin, not_1_out, not_2_out, not_3_out, not_4_out, not_5_out,
       not_6_out, not_7_out, not_8_out, not_9_out, not_10_out, not_11_out, not_12_out, not_13_out,
       not_14_out, not_15_out, not_16_out, not_17_out, not_18_out, not_19_out, not_20_out, not_21_out,
       not_22_out, not_23_out, not_24_out, not_25_out, not_26_out, not_27_out, not_28_out, not_29_out,
       not_30_out, not_31_out, not_32_out, not_33_out, not_34_out, not_35_out, not_36_out, not_37_out,
       not_38_out, not_39_out, not_40_out, not_41_out, not_42_out, or_1_out, or_2_out, or_3_out, or_4_out,
       or_7_out, or_8_out, or_9_out, or_10_out, or_11_out, or_12_out, or_13_out, or_14_out, or_15_out,
       or_16_out, or_17_out, or_18_out, or_19_out, or_20_out, or_21_out, or_22_out, or_23_out, or_24_out,
       or_25_out, or_26_out, or_27_out, or_28_out, or_29_out, or_30_out, or_31_out, or_32_out, or_33_out,
       or_34_out, or_35_out, or_36_out, or_37_out, or_39_out, or_40_out, or_41_out, reset, retenu, tru1,
       tru2, tru4, tru8, tru16, xor_1_out, xor_2_out, xor_3_out, xor_4_out, xor_5_out, xor_6_out, xor_7_out,
       xor_8_out, xor_9_out, xor_10_out, xor_11_out, xor_12_out, xor_13_out, xor_14_out, xor_15_out,
       xor_16_out, xor_17_out, xor_18_out, xor_19_out, xor_20_out, xor_21_out, xor_22_out, xor_23_out,
       xor_24_out, xor_25_out, xor_26_out, z1, z2, z4, z8;

  Button button_1 (.out(b_plus));
  Button button_2 (.out(reset));
  Button button_3 (.out(_1));
  Button button_4 (.out(_4));
  Button button_5 (.out(_7));
  Button button_6 (.out(_2));
  Button button_7 (.out(_5));
  Button button_8 (.out(_8));
  Button button_9 (.out(_0));
  Button button_10 (.out(dt));
  Button button_11 (.out(_3));
  Button button_12 (.out(_6));
  Button button_13 (.out(_9));
  or or_1 (or_1_out, _8, _9);
  or or_2 (or_2_out, _4, _6, _7, _5);
  or or_3 (or_3_out, _2, _6, _7, _3);
  or or_4 (or_4_out, _1, _7, _9, _5, _3);
  D_Flip_Flop #(.Pre_Clr_Positions("LEGACY")) d_ff_1 (
    .Q(d_ff_1_q), .Qn(d_ff_1_qn), .preset(b_plus), .reset(reset));  // open: clk, D
  and and_1 (and_1_out, _0, d_ff_1_qn);
  and and_2 (and_2_out, d_ff_1_q, _0);
  or or_5 (bt, and_1_out, b1, b2, b4, b8);
  and and_3 (b8, or_1_out, d_ff_1_qn);
  and and_4 (b4, or_2_out, d_ff_1_qn);
  and and_5 (b2, or_3_out, d_ff_1_qn);
  and and_6 (b1, or_4_out, d_ff_1_qn);
  and and_7 (c8, or_1_out, d_ff_1_q);
  and and_8 (c4, or_2_out, d_ff_1_q);
  and and_9 (c2, or_3_out, d_ff_1_q);
  and and_10 (c1, or_4_out, d_ff_1_q);
  or or_6 (ct, and_2_out, c1, c2, c4, c8);
  and and_11 (and_11_out, bt, and_27_out);
  and and_12 (and_12_out, xor_2_out, d_ff_5_qn);
  and and_13 (and_13_out, bt, and_28_out);
  and and_14 (and_14_out, xor_3_out, d_ff_8_qn);
  and and_15 (and_15_out, b8, xor_1_out);
  and and_16 (and_16_out, b4, xor_1_out);
  and and_17 (and_17_out, b2, xor_1_out);
  and and_18 (and_18_out, b1, xor_1_out);
  and and_19 (and_19_out, b8, and_12_out);
  and and_20 (and_20_out, b4, and_12_out);
  and and_21 (and_21_out, b2, and_12_out);
  and and_22 (and_22_out, b1, and_12_out);
  and and_23 (and_23_out, b8, and_14_out);
  and and_24 (and_24_out, b4, and_14_out);
  and and_25 (and_25_out, b2, and_14_out);
  and and_26 (and_26_out, b1, and_14_out);
  D_Flip_Flop #(.Pre_Clr_Positions("LEGACY")) d_ff_2 (.Q(d_ff_2_q), .preset(bt), .reset(reset));  // open: clk, D, Qn
  D_Flip_Flop #(.Pre_Clr_Positions("LEGACY")) d_ff_3 (
    .Q(d_ff_3_q), .preset(and_16_out), .reset(reset));  // open: clk, D, Qn
  D_Flip_Flop #(.Pre_Clr_Positions("LEGACY")) d_ff_4 (
    .Q(d_ff_4_q), .preset(and_18_out), .reset(reset));  // open: clk, D, Qn
  D_Flip_Flop #(.Pre_Clr_Positions("LEGACY")) d_ff_5 (
    .Q(d_ff_5_q), .Qn(d_ff_5_qn), .preset(and_11_out), .reset(reset));  // open: clk, D
  D_Flip_Flop #(.Pre_Clr_Positions("LEGACY")) d_ff_6 (
    .Q(d_ff_6_q), .preset(and_20_out), .reset(reset));  // open: clk, D, Qn
  D_Flip_Flop #(.Pre_Clr_Positions("LEGACY")) d_ff_7 (
    .Q(d_ff_7_q), .preset(and_22_out), .reset(reset));  // open: clk, D, Qn
  D_Flip_Flop #(.Pre_Clr_Positions("LEGACY")) d_ff_8 (
    .Q(d_ff_8_q), .Qn(d_ff_8_qn), .preset(and_13_out), .reset(reset));  // open: clk, D
  D_Flip_Flop #(.Pre_Clr_Positions("LEGACY")) d_ff_9 (
    .Q(d_ff_9_q), .preset(and_24_out), .reset(reset));  // open: clk, D, Qn
  D_Flip_Flop #(.Pre_Clr_Positions("LEGACY")) d_ff_10 (
    .Q(d_ff_10_q), .preset(and_26_out), .reset(reset));  // open: clk, D, Qn
  xor xor_1 (xor_1_out, 1'b1, d_ff_2_q);
  D_Flip_Flop #(.Pre_Clr_Positions("LEGACY")) d_ff_11 (
    .Q(d_ff_11_q), .preset(and_15_out), .reset(reset));  // open: clk, D, Qn
  D_Flip_Flop #(.Pre_Clr_Positions("LEGACY")) d_ff_12 (
    .Q(d_ff_12_q), .preset(and_17_out), .reset(reset));  // open: clk, D, Qn
  xor xor_2 (xor_2_out, and_27_out, d_ff_5_q);
  D_Flip_Flop #(.Pre_Clr_Positions("LEGACY")) d_ff_13 (
    .Q(d_ff_13_q), .preset(and_19_out), .reset(reset));  // open: clk, D, Qn
  D_Flip_Flop #(.Pre_Clr_Positions("LEGACY")) d_ff_14 (
    .Q(d_ff_14_q), .preset(and_21_out), .reset(reset));  // open: clk, D, Qn
  xor xor_3 (xor_3_out, and_28_out, d_ff_8_q);
  D_Flip_Flop #(.Pre_Clr_Positions("LEGACY")) d_ff_15 (
    .Q(d_ff_15_q), .preset(and_23_out), .reset(reset));  // open: clk, D, Qn
  D_Flip_Flop #(.Pre_Clr_Positions("LEGACY")) d_ff_16 (
    .Q(d_ff_16_q), .preset(and_25_out), .reset(reset));  // open: clk, D, Qn
  and and_27 (and_27_out, d_ff_2_q, not_1_out);
  not not_1 (not_1_out, bt);
  and and_28 (and_28_out, d_ff_5_q, not_2_out);
  not not_2 (not_2_out, bt);
  D_Flip_Flop #(.Pre_Clr_Positions("LEGACY")) d_ff_17 (
    .Q(d_ff_17_q), .preset(dt), .reset(or_7_out));  // open: clk, D, Qn
  or or_7 (or_7_out, reset, or_9_out);
  and and_29 (and_29_out, fin, d_ff_11_q);
  and and_30 (and_30_out, fin, d_ff_3_q);
  and and_31 (and_31_out, fin, d_ff_12_q);
  and and_32 (and_32_out, fin, d_ff_4_q);
  and and_33 (and_33_out, d_ff_20_q, d_ff_13_q);
  and and_34 (and_34_out, d_ff_20_q, d_ff_6_q);
  and and_35 (and_35_out, d_ff_20_q, d_ff_14_q);
  and and_36 (and_36_out, d_ff_20_q, d_ff_7_q);
  not not_3 (not_3_out, dt);
  and and_37 (and_37_out, d_ff_17_q, d_ff_15_q);
  and and_38 (and_38_out, d_ff_17_q, d_ff_9_q);
  and and_39 (and_39_out, d_ff_17_q, d_ff_16_q);
  and and_40 (and_40_out, d_ff_17_q, d_ff_10_q);
  and and_41 (and_41_out, d_ff_20_q, not_4_out);
  not not_4 (not_4_out, dt);
  D_Flip_Flop #(.Pre_Clr_Positions("LEGACY")) d_ff_18 (
    .Q(d_ff_18_q), .preset(and_42_out), .reset(reset));  // open: clk, D, Qn
  and and_42 (and_42_out, d_ff_17_q, not_3_out);
  and and_43 (and_43_out, d_ff_19_q, dt);
  D_Flip_Flop #(.Pre_Clr_Positions("LEGACY")) d_ff_19 (
    .Q(d_ff_19_q), .preset(and_41_out), .reset(reset));  // open: clk, D, Qn
  D_Flip_Flop #(.Pre_Clr_Positions("LEGACY")) d_ff_20 (
    .Q(d_ff_20_q), .Qn(d_ff_20_qn), .preset(and_44_out), .reset(or_8_out));  // open: clk, D
  and and_44 (and_44_out, d_ff_18_q, dt);
  or or_8 (or_8_out, reset, fin);
  or or_9 (or_9_out, fin, d_ff_20_q);
  or or_10 (or_10_out, and_37_out, or_11_out);
  D_Flip_Flop #(.Pre_Clr_Positions("LEGACY")) d_ff_21 (
    .Q(fin), .Qn(d_ff_21_qn), .preset(and_43_out), .reset(reset));  // open: clk, D
  or or_11 (or_11_out, and_33_out, and_29_out);
  or or_12 (or_12_out, and_34_out, and_30_out);
  or or_13 (or_13_out, and_35_out, and_31_out);
  or or_14 (or_14_out, and_36_out, and_32_out);
  or or_15 (or_15_out, and_38_out, or_12_out);
  or or_16 (or_16_out, and_39_out, or_13_out);
  or or_17 (or_17_out, and_40_out, or_14_out);
  and and_45 (and_45_out, c8, xor_4_out);
  and and_46 (and_46_out, c4, xor_4_out);
  and and_47 (and_47_out, c2, xor_4_out);
  and and_48 (and_48_out, c1, xor_4_out);
  and and_49 (and_49_out, ct, and_75_out);
  and and_50 (and_50_out, xor_5_out, d_ff_25_qn);
  and and_51 (and_51_out, c8, and_50_out);
  and and_52 (and_52_out, c4, and_50_out);
  and and_53 (and_53_out, c2, and_50_out);
  and and_54 (and_54_out, c1, and_50_out);
  and and_55 (and_55_out, ct, and_80_out);
  and and_56 (and_56_out, xor_6_out, d_ff_28_qn);
  and and_57 (and_57_out, c8, and_56_out);
  and and_58 (and_58_out, c4, and_56_out);
  and and_59 (and_59_out, c2, and_56_out);
  and and_60 (and_60_out, c1, and_56_out);
  not not_5 (not_5_out, tru16);
  not not_6 (not_6_out, tru1);
  not not_7 (not_7_out, tru4);
  D_Flip_Flop #(.Pre_Clr_Positions("LEGACY")) d_ff_22 (.Q(d_ff_22_q), .preset(ct), .reset(reset));  // open: clk, D, Qn
  D_Flip_Flop #(.Pre_Clr_Positions("LEGACY")) d_ff_23 (
    .Q(d_ff_23_q), .preset(and_46_out), .reset(reset));  // open: clk, D, Qn
  D_Flip_Flop #(.Pre_Clr_Positions("LEGACY")) d_ff_24 (
    .Q(d_ff_24_q), .preset(and_48_out), .reset(reset));  // open: clk, D, Qn
  D_Flip_Flop #(.Pre_Clr_Positions("LEGACY")) d_ff_25 (
    .Q(d_ff_25_q), .Qn(d_ff_25_qn), .preset(and_49_out), .reset(reset));  // open: clk, D
  D_Flip_Flop #(.Pre_Clr_Positions("LEGACY")) d_ff_26 (
    .Q(d_ff_26_q), .preset(and_52_out), .reset(reset));  // open: clk, D, Qn
  D_Flip_Flop #(.Pre_Clr_Positions("LEGACY")) d_ff_27 (
    .Q(d_ff_27_q), .preset(and_54_out), .reset(reset));  // open: clk, D, Qn
  D_Flip_Flop #(.Pre_Clr_Positions("LEGACY")) d_ff_28 (
    .Q(d_ff_28_q), .Qn(d_ff_28_qn), .preset(and_55_out), .reset(reset));  // open: clk, D
  D_Flip_Flop #(.Pre_Clr_Positions("LEGACY")) d_ff_29 (
    .Q(d_ff_29_q), .preset(and_58_out), .reset(reset));  // open: clk, D, Qn
  D_Flip_Flop #(.Pre_Clr_Positions("LEGACY")) d_ff_30 (
    .Q(d_ff_30_q), .preset(and_60_out), .reset(reset));  // open: clk, D, Qn
  and and_61 (and_61_out, not_5_out, not_6_out, not_7_out, tru2, tru8);
  not not_8 (not_8_out, tru16);
  and and_62 (and_62_out, not_8_out, tru4, tru8, not_9_out, not_10_out);
  not not_9 (not_9_out, tru2);
  not not_10 (not_10_out, tru1);
  not not_11 (not_11_out, tru1);
  and and_63 (and_63_out, not_11_out, tru4, tru8, tru2, not_12_out);
  not not_12 (not_12_out, tru16);
  not not_13 (not_13_out, tru2);
  not not_14 (not_14_out, tru4);
  and and_64 (and_64_out, not_13_out, not_14_out, tru16, not_15_out, not_16_out);
  not not_15 (not_15_out, tru1);
  not not_16 (not_16_out, tru8);
  not not_17 (not_17_out, tru8);
  not not_18 (not_18_out, tru1);
  and and_65 (and_65_out, not_17_out, not_18_out, tru16, tru2, not_19_out);
  not not_19 (not_19_out, tru4);
  xor xor_4 (xor_4_out, 1'b1, d_ff_22_q);
  and and_66 (and_66_out, fin, d_ff_31_q);
  D_Flip_Flop #(.Pre_Clr_Positions("LEGACY")) d_ff_31 (
    .Q(d_ff_31_q), .preset(and_45_out), .reset(reset));  // open: clk, D, Qn
  and and_67 (and_67_out, fin, d_ff_23_q);
  and and_68 (and_68_out, fin, d_ff_32_q);
  D_Flip_Flop #(.Pre_Clr_Positions("LEGACY")) d_ff_32 (
    .Q(d_ff_32_q), .preset(and_47_out), .reset(reset));  // open: clk, D, Qn
  and and_69 (and_69_out, fin, d_ff_24_q);
  not not_20 (not_20_out, ct);
  xor xor_5 (xor_5_out, and_75_out, d_ff_25_q);
  D_Flip_Flop #(.Pre_Clr_Positions("LEGACY")) d_ff_33 (
    .Q(d_ff_33_q), .preset(and_51_out), .reset(reset));  // open: clk, D, Qn
  D_Flip_Flop #(.Pre_Clr_Positions("LEGACY")) d_ff_34 (
    .Q(d_ff_34_q), .preset(and_53_out), .reset(reset));  // open: clk, D, Qn
  not not_21 (not_21_out, ct);
  xor xor_6 (xor_6_out, and_80_out, d_ff_28_q);
  D_Flip_Flop #(.Pre_Clr_Positions("LEGACY")) d_ff_35 (
    .Q(d_ff_35_q), .preset(and_57_out), .reset(reset));  // open: clk, D, Qn
  D_Flip_Flop #(.Pre_Clr_Positions("LEGACY")) d_ff_36 (
    .Q(d_ff_36_q), .preset(and_59_out), .reset(reset));  // open: clk, D, Qn
  not not_22 (not_22_out, tru4);
  not not_23 (not_23_out, tru16);
  and and_70 (and_70_out, not_22_out, not_23_out, tru1, tru2, tru8);
  not not_24 (not_24_out, tru16);
  and and_71 (and_71_out, not_24_out, tru1, tru4, tru8, not_25_out);
  not not_25 (not_25_out, tru2);
  not not_26 (not_26_out, tru16);
  and and_72 (and_72_out, not_26_out, tru1, tru2, tru4, tru8);
  not not_27 (not_27_out, tru4);
  not not_28 (not_28_out, tru8);
  and and_73 (and_73_out, not_27_out, not_28_out, tru16, tru1, not_29_out);
  not not_29 (not_29_out, tru2);
  not not_30 (not_30_out, tru8);
  and and_74 (and_74_out, not_30_out, tru16, tru2, tru1, not_31_out);
  not not_31 (not_31_out, tru4);
  and and_75 (and_75_out, d_ff_22_q, not_20_out);
  and and_76 (and_76_out, d_ff_20_q, d_ff_33_q);
  and and_77 (and_77_out, d_ff_20_q, d_ff_26_q);
  and and_78 (and_78_out, d_ff_20_q, d_ff_34_q);
  and and_79 (and_79_out, d_ff_20_q, d_ff_27_q);
  and and_80 (and_80_out, d_ff_25_q, not_21_out);
  and and_81 (and_81_out, d_ff_17_q, d_ff_35_q);
  and and_82 (and_82_out, d_ff_17_q, d_ff_29_q);
  and and_83 (and_83_out, d_ff_17_q, d_ff_36_q);
  and and_84 (and_84_out, d_ff_17_q, d_ff_30_q);
  or or_18 (or_18_out, and_78_out, and_68_out);
  or or_19 (or_19_out, and_79_out, and_69_out);
  or or_20 (or_20_out, and_77_out, and_67_out);
  or or_21 (or_21_out, or_18_out, and_83_out);
  or or_22 (or_22_out, or_19_out, and_84_out);
  or or_23 (or_23_out, and_76_out, and_66_out);
  or or_24 (or_24_out, or_23_out, and_81_out);
  or or_25 (or_25_out, or_20_out, and_82_out);
  and and_85 (and_85_out, not_33_out, not_32_out);
  not not_32 (not_32_out, and_87_out);
  not not_33 (not_33_out, dt);
  and and_86 (and_86_out, dt, and_85_out);
  and and_87 (and_87_out, or_26_out, not_34_out);
  not not_34 (not_34_out, dt);
  or or_26 (or_26_out, and_63_out, and_61_out, and_70_out, and_62_out, and_71_out, and_72_out, and_64_out, and_73_out, and_65_out, and_74_out);
  and and_88 (and_88_out, and_87_out, dt);
  D_Flip_Flop #(.Pre_Clr_Positions("LEGACY")) d_ff_37 (
    .Q(retenu), .preset(and_88_out), .reset(and_86_out));  // open: clk, D, Qn
  or or_27 (or_27_out, and_70_out, and_71_out, and_74_out, and_73_out, and_72_out);
  or or_28 (or_28_out, and_71_out, and_64_out, and_73_out, and_62_out);
  or or_29 (or_29_out, and_63_out, and_72_out, and_64_out, and_73_out);
  or or_30 (or_30_out, and_65_out, and_74_out);
  and and_89 (and_89_out, or_17_out, retenu);
  and and_90 (and_90_out, or_16_out, in_3);
  and and_91 (and_91_out, or_15_out, in_4);
  and and_92 (and_92_out, or_10_out, in_5);
  and and_93 (and_93_out, dt, and_126_out);
  xor xor_7 (xor_7_out, or_17_out, retenu);
  and and_94 (and_94_out, in_2, xor_7_out);
  xor xor_8 (xor_8_out, or_16_out, in_3);
  and and_95 (and_95_out, or_35_out, xor_8_out);
  xor xor_9 (xor_9_out, or_15_out, in_4);
  and and_96 (and_96_out, or_36_out, xor_9_out);
  xor xor_10 (xor_10_out, or_10_out, in_5);
  and and_97 (and_97_out, or_37_out, xor_10_out);
  or or_31 (or_31_out, and_134_out, or_27_out);
  or or_32 (or_32_out, and_133_out, or_28_out);
  or or_33 (or_33_out, and_131_out, or_29_out);
  or or_34 (or_34_out, and_132_out, or_30_out);
  and and_98 (and_98_out, xor_19_out, d_ff_39_qn);
  and and_99 (and_99_out, z8, and_98_out);
  and and_100 (and_100_out, z4, and_98_out);
  and and_101 (and_101_out, z2, and_98_out);
  and and_102 (and_102_out, z1, and_98_out);
  and and_103 (and_103_out, dt, and_120_out);
  and and_104 (and_104_out, xor_20_out, d_ff_44_qn);
  and and_105 (and_105_out, z8, and_104_out);
  and and_106 (and_106_out, z4, and_104_out);
  and and_107 (and_107_out, z2, and_104_out);
  and and_108 (and_108_out, z1, and_104_out);
  and and_109 (and_109_out, dt, and_121_out);
  and and_110 (and_110_out, xor_21_out, d_ff_49_qn);
  and and_111 (and_111_out, z8, and_110_out);
  and and_112 (and_112_out, z4, and_110_out);
  and and_113 (and_113_out, z2, and_110_out);
  and and_114 (and_114_out, z1, and_110_out);
  xor xor_11 (xor_11_out, in_2, xor_7_out);
  or or_35 (or_35_out, and_94_out, and_89_out);
  xor xor_12 (xor_12_out, or_35_out, xor_8_out);
  or or_36 (or_36_out, and_95_out, and_90_out);
  xor xor_13 (xor_13_out, or_36_out, xor_9_out);
  or or_37 (or_37_out, and_96_out, and_91_out);
  xor xor_14 (xor_14_out, or_37_out, xor_10_out);
  // OR_Gate or_38 has open pins: in0=and_97_out, in1=and_92_out, out=open
  xor xor_15 (xor_15_out, dt, or_31_out);
  and and_115 (z1, xor_15_out, not_35_out);
  not not_35 (not_35_out, dt);
  xor xor_16 (xor_16_out, dt, or_32_out);
  and and_116 (z2, xor_16_out, not_36_out);
  not not_36 (not_36_out, dt);
  xor xor_17 (xor_17_out, dt, or_33_out);
  and and_117 (z4, xor_17_out, not_37_out);
  not not_37 (not_37_out, dt);
  xor xor_18 (xor_18_out, dt, or_34_out);
  and and_118 (z8, xor_18_out, not_38_out);
  not not_38 (not_38_out, dt);
  and and_119 (and_119_out, retenu, fin);
  D_Flip_Flop #(.Pre_Clr_Positions("LEGACY")) d_ff_38 (.Q(d_ff_38_q), .preset(dt), .reset(reset));  // open: clk, D, Qn
  D_Flip_Flop #(.Pre_Clr_Positions("LEGACY")) d_ff_39 (
    .Q(d_ff_39_q), .Qn(d_ff_39_qn), .preset(and_93_out), .reset(reset));  // open: clk, D
  D_Flip_Flop #(.Pre_Clr_Positions("LEGACY")) d_ff_40 (
    .Q(d_ff_40_q), .preset(and_99_out), .reset(reset));  // open: clk, D, Qn
  D_Flip_Flop #(.Pre_Clr_Positions("LEGACY")) d_ff_41 (
    .Q(d_ff_41_q), .preset(and_100_out), .reset(reset));  // open: clk, D, Qn
  D_Flip_Flop #(.Pre_Clr_Positions("LEGACY")) d_ff_42 (
    .Q(d_ff_42_q), .preset(and_101_out), .reset(reset));  // open: clk, D, Qn
  D_Flip_Flop #(.Pre_Clr_Positions("LEGACY")) d_ff_43 (
    .Q(d_ff_43_q), .preset(and_102_out), .reset(reset));  // open: clk, D, Qn
  D_Flip_Flop #(.Pre_Clr_Positions("LEGACY")) d_ff_44 (
    .Q(d_ff_44_q), .Qn(d_ff_44_qn), .preset(and_103_out), .reset(reset));  // open: clk, D
  D_Flip_Flop #(.Pre_Clr_Positions("LEGACY")) d_ff_45 (
    .Q(d_ff_45_q), .preset(and_105_out), .reset(reset));  // open: clk, D, Qn
  D_Flip_Flop #(.Pre_Clr_Positions("LEGACY")) d_ff_46 (
    .Q(d_ff_46_q), .preset(and_106_out), .reset(reset));  // open: clk, D, Qn
  D_Flip_Flop #(.Pre_Clr_Positions("LEGACY")) d_ff_47 (
    .Q(d_ff_47_q), .preset(and_107_out), .reset(reset));  // open: clk, D, Qn
  D_Flip_Flop #(.Pre_Clr_Positions("LEGACY")) d_ff_48 (
    .Q(d_ff_48_q), .preset(and_108_out), .reset(reset));  // open: clk, D, Qn
  D_Flip_Flop #(.Pre_Clr_Positions("LEGACY")) d_ff_49 (
    .Q(d_ff_49_q), .Qn(d_ff_49_qn), .preset(and_109_out), .reset(reset));  // open: clk, D
  D_Flip_Flop #(.Pre_Clr_Positions("LEGACY")) d_ff_50 (
    .Q(d_ff_50_q), .preset(and_111_out), .reset(reset));  // open: clk, D, Qn
  D_Flip_Flop #(.Pre_Clr_Positions("LEGACY")) d_ff_51 (
    .Q(d_ff_51_q), .preset(and_112_out), .reset(reset));  // open: clk, D, Qn
  D_Flip_Flop #(.Pre_Clr_Positions("LEGACY")) d_ff_52 (
    .Q(d_ff_52_q), .preset(and_113_out), .reset(reset));  // open: clk, D, Qn
  D_Flip_Flop #(.Pre_Clr_Positions("LEGACY")) d_ff_53 (
    .Q(d_ff_53_q), .preset(and_114_out), .reset(reset));  // open: clk, D, Qn
  xor xor_19 (xor_19_out, and_126_out, d_ff_39_q);
  not not_39 (not_39_out, dt);
  xor xor_20 (xor_20_out, and_120_out, d_ff_44_q);
  not not_40 (not_40_out, dt);
  xor xor_21 (xor_21_out, and_121_out, d_ff_49_q);
  not not_41 (not_41_out, dt);
  xor xor_22 (xor_22_out, dt, d_ff_38_q);
  and and_120 (and_120_out, d_ff_39_q, not_39_out);
  and and_121 (and_121_out, d_ff_44_q, not_40_out);
  xor xor_23 (xor_23_out, or_22_out, xor_11_out);
  and and_122 (and_122_out, or_22_out, xor_11_out);
  xor xor_24 (xor_24_out, or_21_out, xor_12_out);
  and and_123 (and_123_out, or_21_out, xor_12_out);
  xor xor_25 (xor_25_out, or_25_out, xor_13_out);
  and and_124 (and_124_out, or_25_out, xor_13_out);
  xor xor_26 (xor_26_out, or_24_out, xor_14_out);
  and and_125 (and_125_out, or_24_out, xor_14_out);
  and and_126 (and_126_out, not_41_out, xor_22_out);
  and and_127 (and_127_out, in_1, xor_23_out);
  and and_128 (and_128_out, or_39_out, xor_24_out);
  and and_129 (and_129_out, or_40_out, xor_25_out);
  and and_130 (and_130_out, or_41_out, xor_26_out);
  xor xor_27 (tru1, in_1, xor_23_out);
  or or_39 (or_39_out, and_127_out, and_122_out);
  xor xor_28 (tru2, or_39_out, xor_24_out);
  or or_40 (or_40_out, and_128_out, and_123_out);
  xor xor_29 (tru4, or_40_out, xor_25_out);
  or or_41 (or_41_out, and_129_out, and_124_out);
  xor xor_30 (tru8, or_41_out, xor_26_out);
  or or_42 (tru16, and_130_out, and_125_out);
  not not_42 (not_42_out, or_26_out);
  and and_131 (and_131_out, not_42_out, tru4);
  and and_132 (and_132_out, not_42_out, tru8);
  and and_133 (and_133_out, not_42_out, tru2);
  and and_134 (and_134_out, not_42_out, tru1);

  // Other names for the same wires on the sheet: tunnel = dt

  // Notes on the sheet:
  //   8
  //   4
  //   2
  //   1
  //   2
  //   8
  //   4
  //   1
  //   retarde le signal jusqu'a le signal est laché
  //   retarde le signal jusqu'a le signal est laché
  //   1
  //   2
  //   4
  //   8
  //   b
  //   a
  //   1
  //   2
  //   4
  //   8
  //   1
  //   2
  //   4
  //   8
  //   8
  //   4
  //   2
  //   1
  //   retarde le signal jusqu'a le signal est laché
  //   retarde le signal jusqu'a le signal est laché
  //   1
  //   2
  //   4
  //   8
  //   16
endmodule
